# Fritzing sketch Diagram (saved by Fritzing 0.9.3b)
breadboards: 1

parts:
  Part1 = Arduino Mega 2560 (Rev3)
  C1 = Electrolytic Capacitor [capacitance=0.1mF package="100 mil [THT, electrolytic]"]
  R1 = Resistor [tolerance=±5% resistance=220 package=THT]
  Power_plug1 = Power plug
  Part2 = ws2812b [package="smd 2812b"]
  VCC1 = 4 x AAA Battery Mount

nets:
  GND: Part1.GND, C1.-, Power_plug1.GND, Part2.VSS, VCC1.-
  N1: Part1.VIN, VCC1.+
  N2: Part1.D5_PWM, R1.Pin_1
  VCC: C1.+, Power_plug1.VCC, Part2.VDD
  N3: R1.Pin_0, Part2.DIN
